# Fritzing sketch Carduino_frintzing_2 (saved by Fritzing 0.9.3b)
circuit board: 8.46667cm x 5.64444cm
breadboards: 3

parts:
  Part1 = Arduino Mega 2560 (Rev3)
  Part2 = Adafruit Motor/Stepper/Servo Shield [part_number="Adafruit #1438"]
  hc-sr1 = hc-sr04
  hc-sr2 = hc-sr04
  hc-sr3 = hc-sr04
  SPKR1 = Loudspeaker
  R1 = Resistor [tolerance=±5% resistance=100 package="2010 [SMD]"]
  M1 = DC Motor  # not connected
  IR1 = TSOP312.., 314.. [package=THT]
  M2 = DC Motor  # not connected
  VCC1 = 4 x AAA Battery Mount
  S2 = SPST Switch [package=r_sw_th]
  JACK1 = 2.1mm Barrel Jack with Terminal Block
  VCC2 = Battery block 9V
  S3 = SPST Switch [package=r_sw_th]

nets:
  GND: Part1.GND, hc-sr1.GND, hc-sr2.GND, hc-sr3.GND, IR1.GND
  VCC: Part1.5V, hc-sr1.VCC, hc-sr2.VCC, hc-sr3.VCC, IR1.Vs
  N1: Part1.D24, IR1.Data
  N2: Part1.D33, hc-sr2.Echo
  N3: Part1.D35, hc-sr2.Trig
  N4: Part1.D39, hc-sr3.Echo
  N5: Part1.D41, hc-sr3.Trig
  N6: Part1.D45, hc-sr1.Echo
  N7: Part1.D47, hc-sr1.Trig
  N8: Part2.D12, SPKR1.pin1
  N9: Part2.GND, S2.O
  N10: Part2.VMOTOR, VCC1.+
  N11: Part2.D11, R1.Pin_1
  N12: SPKR1.pin2, R1.Pin_0
  N13: VCC1.-, S2.P
  N14: JACK1.POS, VCC2.+
  N15: JACK1.NEG, S3.O
  N16: VCC2.-, S3.P

notes:
  Ir reciever
  Ultrasonic tranciever
  DC motor
  9V source for Arduino board
  4.5V source for DC motors
  Adafruit Motor Shield power switch
  Arduino board power switch
  piezoelectric speaker
  Arduino Mega 2560
  Adafruit Motor Shield v2

custom parts:
  Adafruit Motor/Stepper/Servo Shield: The original Adafruit Motorshield kit is one of our most beloved kits, which is why we decided to make something even better. We have upgraded the shield kit to make the bestest, easiest way to drive DC and Stepper motors. This shield will make quick work of your next robotics project! We kept the ability to drive up to 4 DC motors or 2 stepper motors, but added many improvements: Instead of a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

// code stored in the sketch: Carduino.ino
/**
 * @file Carduino.ino
 * @Author David Kunz
 * @date March, 2017
 * @brief Code running on the Arduino Mega unit.
 */

//include used libraries:
#include <IRremote.h> //IR reciever library (https://github.com/z3t0/Arduino-IRremote)
#include <PrintEx.h> //StreamEx library (used because of the lack of pritf in Arduino) (https://github.com/Chris--A/PrintEx)
#include <NewPing.h> //Ultrasonic library (https://bitbucket.org/teckel12/arduino-new-ping/wiki/Home)
#include <toneAC.h> //use pins 11 & 12 pwm (https://bitbucket.org/teckel12/arduino-toneac/wiki/Home)
#include <Wire.h> //Two Wire Interface (TWI/I2C)(used by the Adafruit Motor Shield) (http://playground.arduino.cc/Main/WireLibraryDetailedReference)
#include <Adafruit_MotorShield.h> //AdafruitMotorShield library (https://learn.adafruit.com/adafruit-motor-shield-v2-for-arduino/library-reference)

//logging
StreamEx mySerial = Serial;
void log(String command, boolean logOn = true);
boolean loggingOn = true;

// ultrasonic variables
#define NUMBER_OF_SONARS 3
#define MAX_MEASURE_DISTANCE 200 // Maximum distance (in cm) to ping.
NewPing sonar[NUMBER_OF_SONARS] = {   // Sensor object array.
  NewPing(35, 33, MAX_MEASURE_DISTANCE), //left sonar
  NewPing(41, 39, MAX_MEASURE_DISTANCE), // middle sonar
  NewPing(47, 45, MAX_MEASURE_DISTANCE)  //right sonar
};
int distance[NUMBER_OF_SONARS];

//motorshield object
Adafruit_MotorShield AFMS = Adafruit_MotorShield();
Adafruit_DCMotor *motorL = AFMS.getMotor(1);
Adafruit_DCMotor *motorR = AFMS.getMotor(2);

//motor variables
float speedRightCoefficient = 0.0;
float speedLeftCoefficient = 0.0;
uint8_t directionRight = RELEASE;
uint8_t directionLeft = RELEASE;

//IR reciever
#define RECEIVER_PIN 24
IRrecv irrecv(RECEIVER_PIN);
decode_results results;

//gear speed
int motorSpeed = 150;
/**
 * [setMovementVars description]
 * @param spdL   [description]
 * @param spdR   [description]
 * @param direcL [description]
 * @param direcR [description]
 */
void setMovementVars(float spdL, float spdR, uint8_t direcL, uint8_t direcR){
  speedLeftCoefficient = spdL;
  speedRightCoefficient = spdR;
  directionLeft = direcL;
  directionRight = direcR;
}

void log(String command, boolean logOn = true){
  if (logOn == true){
    float secs = millis()/1000.0;
    Serial.println(command);
    mySerial.printf("Data:\t(%.1f)\n\tSpeedLeftCoefficient: %.2f\n\tspeedRightCoefficient: %.2f\n\tdistance Left: %d\n\tdistance Middle: %d\n\tdistance Right: %d\n",
                                secs, speedLeftCoefficient, speedRightCoefficient, distance[0], distance[1], distance[2]);
  }
}

void updateDistance(){
  for (uint8_t i = 0; i < NUMBER_OF_SONARS; i++){
    distance[i] = sonar[i].ping_cm();
    delay(15); //it takes 11,8ms for signal that bounces off an obstacle 200cm away to return
  }
}

void runMotors(float spdPer){
  motorR->setSpeed(speedRightCoefficient*motorSpeed*spdPer);
  motorL->setSpeed(speedLeftCoefficient*motorSpeed*spdPer);
  motorR->run(directionRight);
  motorL->run(directionLeft);
}

class ChangeSpeed
{
	float speedPercentage;
	int changeSpeedDistance;
  int endChangeSpeedDistance;
	int resetTime;
  boolean disableChangeSpeed;
	unsigned long previousMillis;  	//stores when them speed was last modified

  // Constructor - creates a ChangeSpeedAt
  // and initializes the member variables and state

  //tone variables
  //toneAC( frequency [, volume [, length [, background ]]] )
  int toneFrequency;
  int toneVolume;
  int toneLength;

  public:
  ChangeSpeed(int changeSpeeddDis, int endChangeSpeedDis, int toneFreq, float speedPer) //add tone variables
    : speedPercentage(speedPer),
      changeSpeedDistance(changeSpeeddDis),
      endChangeSpeedDistance(endChangeSpeedDis),
      resetTime(5000),
      disableChangeSpeed(false),
      previousMillis(0),
      toneFrequency(toneFreq),
      toneVolume(8),
      toneLength(2)
  {
    /*
    changeSpeedDistance = chSpdDis;
    resetTime = resTime*1000;
    speedPercentage = spdPer;

  	previousMillis = 0;
    disableChangeSpeed = false;
    */
  }

  void CheckForObstacle(){ //checks for an obstacle for the actual object if its within changeSpeedDistance it makes a sound and changes the speed to speedPercentage
    unsigned long currentMillis = millis();
    if((0 < distance[0] && distance[0] <= changeSpeedDistance && endChangeSpeedDistance < distance[0]) || (0 < distance[1] && distance[1] <= changeSpeedDistance && endChangeSpeedDistance < distance[1]) || (0 < distance[2] && distance[2] <= changeSpeedDistance && endChangeSpeedDistance < distance[2])){
      //add tone here
      toneAC(toneFrequency, toneVolume, toneLength);
      if(disableChangeSpeed == false){
        runMotors(speedPercentage);
        disableChangeSpeed = true;
        previousMillis = currentMillis;
        log("EVENT: Change speed");
      }
    } else if(currentMillis - previousMillis >= resetTime){
      disableChangeSpeed = false;
    }
  }
};

ChangeSpeed slow(35, 20, 3000, 0.5);
ChangeSpeed stop(20, 0, 3500, 0.0);

void setup() {
  Serial.begin(9600);

  //motors
  AFMS.begin();

  //IR reciever
  irrecv.enableIRIn();
}

void loop() {

  if (irrecv.decode(&results)) {
    switch (results.value){
      case 0xFF18E7: // Go straight (button ▲)
        setMovementVars(1.0, 1.0, FORWARD, FORWARD);
        log("CMD: Go straight", loggingOn);
        break;
      case 0xFF5AA5: // Turn right (button ►)
        setMovementVars(1.0, 1.0/3.0, FORWARD, FORWARD);
        log("CMD: Turn right", loggingOn);
        break;
      case 0xFF10EF: // Turn left (button ◄)
        setMovementVars(1.0/3.0, 1.0, FORWARD, FORWARD);
        log("CMD: Turn left", loggingOn);
        break;
      case 0xFF4AB5: // Go backwards (button ▼)
        setMovementVars(2.0/3.0, 2.0/3.0, BACKWARD, BACKWARD);
        log("CMD: Go backward", loggingOn);
        break;
      case 0xFF38C7: // release (button OK)
        setMovementVars(0.0, 0.0, RELEASE, RELEASE);
        break;
      //CHANGE SPEED:
      case 0xFFA25D: // speed gear 1 (button 1)
        motorSpeed = 43;
        log("CMD: Gear 1", loggingOn);
        break;
      case 0xFF629D: // speed gear 2 (button 2)
        motorSpeed = 85;
        log("CMD: Gear 2", loggingOn);
        break;
      case 0xFFE21D: // speed gear 3 (button 3)
        motorSpeed = 128;
        log("CMD: Gear 3", loggingOn);
        break;
      case 0xFF22DD: // speed gear 4 (button 4)
        motorSpeed = 170;
        log("CMD: Gear 4", loggingOn);
        break;
      case 0xFF02FD: // speed gear 5 (button 5)
        motorSpeed = 213;
        log("CMD: Gear 5", loggingOn);
        break;
      case 0xFFC23D: // speed gear 6 (button 6)
        motorSpeed = 255;
        log("CMD: Gear 6", loggingOn);
        break;
      case 0xFF6897: // slow down (button *)
        motorSpeed = motorSpeed - 20;
        if(motorSpeed < 0) motorSpeed = 0;
        break;
      case 0xFFB04F: // speed up (button #)
        motorSpeed = motorSpeed + 20;
        if(motorSpeed > 255) motorSpeed = 255;
        break;
      case 0xFFE01F: // print everything (button 7)
        log("CMD: Check data");
        break;
    }
    runMotors(1.0);

    irrecv.resume();
  }

  updateDistance();

  slow.CheckForObstacle();
  stop.CheckForObstacle();
}
